// Logisim project Guia_1302.circ as structural Verilog: 1 circuit, main circuit main
module main (
  input  pulse,
  input  in_2,
  input  CLR,
  output out_4,
  output out_5,
  output out_6,
  output out_7,
  output out_8
);

  wire j_k_ff_2_q, j_k_ff_3_q, j_k_ff_4_q, j_k_ff_5_q;

  J_K_Flip_Flop j_k_ff_1 (.J(in_2), .clk(j_k_ff_2_q), .K(in_2), .Qn(out_4), .reset(CLR));  // open: Q, preset, en
  J_K_Flip_Flop j_k_ff_2 (
    .J(in_2), .clk(j_k_ff_3_q), .K(in_2), .Q(j_k_ff_2_q), .Qn(out_5), .reset(CLR));  // open: preset, en
  J_K_Flip_Flop j_k_ff_3 (
    .J(in_2), .clk(j_k_ff_4_q), .K(in_2), .Q(j_k_ff_3_q), .Qn(out_6), .reset(CLR));  // open: preset, en
  J_K_Flip_Flop j_k_ff_4 (
    .J(in_2), .clk(j_k_ff_5_q), .K(in_2), .Q(j_k_ff_4_q), .Qn(out_7), .reset(CLR));  // open: preset, en
  J_K_Flip_Flop j_k_ff_5 (
    .J(in_2), .clk(pulse), .K(in_2), .Q(j_k_ff_5_q), .Qn(out_8), .reset(CLR));  // open: preset, en
endmodule
