// Logisim project Guia_1303.circ as structural Verilog: 1 circuit, main circuit main
module main (
  input  in_1,
  input  pulse,
  input  CLR,
  output out_4,
  output out_5,
  output out_6,
  output out_7
);

  wire j_k_ff_1_qn, j_k_ff_2_qn, j_k_ff_3_qn, nand_1_out, nand_2_out;

  nand nand_1 (nand_1_out, out_7, out_6, out_5, out_4);
  J_K_Flip_Flop j_k_ff_1 (
    .J(in_1), .clk(pulse), .K(in_1), .Q(out_7), .Qn(j_k_ff_1_qn), .reset(nand_2_out));  // open: preset, en
  nand nand_2 (nand_2_out, CLR, nand_1_out);
  J_K_Flip_Flop j_k_ff_2 (
    .J(in_1), .clk(j_k_ff_1_qn), .K(in_1), .Q(out_6), .Qn(j_k_ff_2_qn), .reset(nand_2_out));  // open: preset, en
  J_K_Flip_Flop j_k_ff_3 (
    .J(in_1), .clk(j_k_ff_2_qn), .K(in_1), .Q(out_5), .Qn(j_k_ff_3_qn), .reset(nand_2_out));  // open: preset, en
  J_K_Flip_Flop j_k_ff_4 (
    .J(in_1), .clk(j_k_ff_3_qn), .K(in_1), .Q(out_4), .reset(nand_2_out));  // open: Qn, preset, en
endmodule
