// Logisim project Guia_1403.circ as structural Verilog: 1 circuit, main circuit main
module main (
  input  CLK,
  input  in_2,
  input  CLR,
  output out_4,
  output out_5,
  output out_6,
  output out_7
);

  wire or_1_out;

  or or_1 (or_1_out, in_2, out_7);
  D_Flip_Flop d_ff_1 (.clk(CLK), .D(or_1_out), .Q(out_4), .reset(CLR));  // open: Qn, preset, en
  D_Flip_Flop d_ff_2 (.clk(CLK), .D(out_4), .Q(out_5), .reset(CLR));  // open: Qn, preset, en
  D_Flip_Flop d_ff_3 (.clk(CLK), .D(out_5), .Q(out_6), .reset(CLR));  // open: Qn, preset, en
  D_Flip_Flop d_ff_4 (.clk(CLK), .D(out_6), .Q(out_7), .reset(CLR));  // open: Qn, preset, en
endmodule
